# Fritzing sketch natal esquematico (saved by Fritzing 0.9.1b)
breadboards: 1

parts:
  Part1 = Arduino Uno (Rev3)
  SP1 = SPEAKER [package=pcb_mount_speaker]
  LED1 = smd LED [color="Red (633nm)" package="0603 [SMD]"]
  LED2 = smd LED [color="Red (633nm)" package="0603 [SMD]"]
  R1 = Resistor [tolerance=±5% resistance=220 package="0805 [SMD]"]
  R2 = Resistor [tolerance=±5% resistance=220 package="0805 [SMD]"]

nets:
  N1: Part1.D9_PWM, SP1.-
  N2: Part1.GND, SP1.+, LED1.cathode
  N3: Part1.D2, R2.Pin_0
  N4: Part1.D3_PWM, R1.Pin_0
  N5: LED1.anode, R2.Pin_1
  N6: LED2.anode, R1.Pin_1
